# Fritzing sketch beadando_sketch_10_12 (saved by Fritzing 0.9.3b)
breadboards: 1

parts:
  U2 = RELAY [package=relay-jzc]
  U3 = RELAY [package=relay-jzc]
  U4 = RELAY [package=relay-jzc]
  Part1 = Arduino Uno (Rev3)
  IR1 = TSOP312.., 314.. [package=THT]
  Part2 = Bluetooth HC-05 Macho
  J1 = Piezo Speaker
  R1 = PHOTOCELL [package=photocell]
  J2 = Camdenboss CTB0158-4 [part_number=CTB0158-4 package=THT]
  LED1 = smd LED [color="Red (633nm)" package="0805 [SMD]"]  # not connected
  LED2 = LEDs [package=led10mm]
  R2 = Resistor [tolerance=±5% resistance=220 package="0402 [SMD]"]  # not connected
  R3 = Resistor [tolerance=±5% resistance=220 package="0402 [SMD]"]
  R4 = Resistor [tolerance=±5% resistance=220 package="0603 [SMD]"]

nets:
  N1: U2.COIL1, Part1.D13/SCK
  5V: U3.NC, Part1.5V, IR1.Vs, Part2.VCC, R1.P$1, J2.terminal_2
  N2: U3.COIL1, Part1.D12/MISO
  N3: U4.COIL1, Part1.D8
  N4: Part1.A0, J2.terminal_4
  N5: Part1.D10_PWM/SS, J1.pin2
  N6: Part1.D11_PWM/MOSI, IR1.Data
  GND: Part1.GND, IR1.GND, Part2.GND, J1.pin1, J2.pin3, R4.Pin_1
  N7: Part1.D0/RX, Part2.TXD
  N8: Part1.D1/TX, Part2.RXD
  N9: Part1.D3_PWM, J2.terminal_1
  N10: R1.P$2, R4.Pin_0
  N11: LED2.A, R3.Pin_0
